# Fritzing sketch R08_N01 (saved by Fritzing 0.9.2b)
breadboards: 1

parts:
  Componente1 = Arduino Uno (Rev3)
  Mod1 = gy-906

nets:
  N1: Componente1.A4/SDA, Mod1.SDA
  N2: Componente1.A5/SCL, Mod1.SCL
  5V: Componente1.5V, Mod1.VIN
  GND: Componente1.GND, Mod1.GND

custom parts:
  gy-906: gy-906 Non-contact PIR I2C interface temperature sensor breakout board.
