# Fritzing sketch R08_N03 (saved by Fritzing 0.9.3b)
breadboards: 1

parts:
  Componente3 = Arduino Uno (Rev3)
  Mod4 = gy-906
  LCD1 = LCD screen
  LCM1602_IIC1 = LCM1602 IIC [part_number="LCM1602 IIC" chip_label="LCM1602 IIC" package="DIP (Dual Inline) [THT]"]
  Mod5 = Full Size SD Card Module

nets:
  N1: Componente3.A4/SDA, Mod4.SDA, LCM1602_IIC1.SDA
  N2: Componente3.A5/SCL, Mod4.SCL, LCM1602_IIC1.SCL
  N3: Componente3.D10_PWM/SS, Mod5.pin_7, Mod5.pin_8
  N4: Componente3.D11_PWM/MOSI, Mod5.pin_9, Mod5.pin_10
  N5: Componente3.D12/MISO, Mod5.pin_13, Mod5.pin_14
  N6: Componente3.D13/SCK, Mod5.pin_11, Mod5.pin_12
  5V: Componente3.5V, Mod4.VIN, LCM1602_IIC1.VCC, Mod5.pin_5, Mod5.pin_6
  GND: Componente3.GND, LCM1602_IIC1.GND, Mod5.pin_1, Mod5.pin_2, Mod5.pin_16
  VSS: LCD1.VSS, LCM1602_IIC1.VSS
  VDD: LCD1.VDD, LCM1602_IIC1.VDD
  N7: LCD1.V0, LCM1602_IIC1.V0
  N8: LCD1.RS, LCM1602_IIC1.RS
  N9: LCD1.R/W, LCM1602_IIC1.RW
  N10: LCD1.E, LCM1602_IIC1.E
  N11: LCD1.DB0, LCM1602_IIC1.D0
  N12: LCD1.DB1, LCM1602_IIC1.D1
  N13: LCD1.DB2, LCM1602_IIC1.D2
  N14: LCD1.DB3, LCM1602_IIC1.D3
  N15: LCD1.DB4, LCM1602_IIC1.D4
  N16: LCD1.DB5, LCM1602_IIC1.D5
  N17: LCD1.DB6, LCM1602_IIC1.D6
  N18: LCD1.DB7, LCM1602_IIC1.D7
  N19: LCD1.LED+, LCM1602_IIC1.A
  N20: LCD1.LED-, LCM1602_IIC1.K
  N21: LCM1602_IIC1.LED_A, LCM1602_IIC1.LED_B

custom parts:
  gy-906: gy-906 Non-contact PIR I2C interface temperature sensor breakout board.
  LCM1602 IIC: I2C-Module to use a 1602 or 2004 LCD on with the wire.h libory Serial LCD Modul
  Full Size SD Card Module: SD Card Module Slot Socket Reader For Arduino ARM MCU
